// Logisim project 4-function-calculator.circ as structural Verilog: 3 circuits, main circuit main
module main (
  input  [3:0] A,
  input  [1:0] in_2,
  input  [3:0] B,
  output [3:0] out_4
);

  wire [1:0] bitselector_1_out;
  wire [3:0] multiplier_1_out, my_4_bit_adder_1_out, my_4_bit_adder_2_out, not_1_out, shifter_1_out;

  BitSelector #(.width(4), .group(2)) bitselector_1 (.in(B), .out(bitselector_1_out), .sel(1'b0));
  my_4_bit_adder my_4_bit_adder_1 (.A(A), .Cin(1'b0), .B(B), .Out(my_4_bit_adder_1_out));  // open: Cout
  assign not_1_out = ~B;  // NOT_Gate not_1, 4 bits wide
  Multiplier #(.width(4)) multiplier_1 (.a(B), .b(A), .out(multiplier_1_out));  // open: cin, cout
  Shifter #(.width(4)) shifter_1 (.in(A), .\dist (bitselector_1_out), .out(shifter_1_out));
  my_4_bit_adder my_4_bit_adder_2 (.A(A), .Cin(1'b1), .B(not_1_out), .Out(my_4_bit_adder_2_out));  // open: Cout
  // Probe on out_4
  Multiplexer #(.select(2), .width(4), .enable("false")) multiplexer_1 (
    .in0(my_4_bit_adder_1_out), .in1(my_4_bit_adder_2_out), .in2(multiplier_1_out), .in3(shifter_1_out),
    .out(out_4), .sel(in_2));
endmodule

module my_1_bit_adder (
  input  A,
  input  B,
  input  Cin,
  output S,
  output Cin_2
);

  wire and_1_out, and_2_out, and_3_out, and_4_out, and_5_out, and_6_out, and_7_out, not_1_out, not_2_out,
       not_3_out, not_4_out, not_5_out, not_6_out;

  not not_1 (not_1_out, A);
  not not_2 (not_2_out, B);
  not not_3 (not_3_out, A);
  not not_4 (not_4_out, Cin);
  not not_5 (not_5_out, B);
  not not_6 (not_6_out, Cin);
  and and_1 (and_1_out, B, Cin);
  and and_2 (and_2_out, A, Cin);
  and and_3 (and_3_out, A, B);
  and and_4 (and_4_out, not_1_out, not_2_out, Cin);
  and and_5 (and_5_out, not_3_out, B, not_4_out);
  and and_6 (and_6_out, A, not_5_out, not_6_out);
  and and_7 (and_7_out, A, B, Cin);
  or or_1 (Cin_2, and_1_out, and_2_out, and_3_out);
  or or_2 (S, and_4_out, and_5_out, and_6_out, and_7_out);
endmodule

module my_4_bit_adder (
  input  [3:0] A,
  input  Cin,
  input  [3:0] B,
  output [3:0] Out,
  output Cout
);

  wire my_1_bit_adder_1_cin_2, my_1_bit_adder_2_cin_2, my_1_bit_adder_3_cin_2;

  my_1_bit_adder my_1_bit_adder_1 (.A(A[0]), .B(B[0]), .Cin(Cin), .S(Out[0]), .Cin_2(my_1_bit_adder_1_cin_2));
  my_1_bit_adder my_1_bit_adder_2 (
    .A(A[1]), .B(B[1]), .Cin(my_1_bit_adder_1_cin_2), .S(Out[1]), .Cin_2(my_1_bit_adder_2_cin_2));
  my_1_bit_adder my_1_bit_adder_3 (
    .A(A[2]), .B(B[2]), .Cin(my_1_bit_adder_2_cin_2), .S(Out[2]), .Cin_2(my_1_bit_adder_3_cin_2));
  my_1_bit_adder my_1_bit_adder_4 (.A(A[3]), .B(B[3]), .Cin(my_1_bit_adder_3_cin_2), .S(Out[3]), .Cin_2(Cout));
endmodule
