// Logisim project cpu.circ as structural Verilog: 8 circuits, main circuit CPU
module CPU (
  output [7:0] PC
);

  wire alu_1_zero_dectector, clock_1_out, control_1_alu_arg2_ram_data_in, control_1_branch, control_1_halt,
       control_1_jump, control_1_put_en, control_1_ram_load, control_1_ram_store, control_1_w_adr,
       control_1_w_en, multiplexer_1_out;
  wire [1:0] control_1_alu_operation_select, control_1_write_data_input_select, instruction_decoder_1_rd,
       instruction_decoder_1_rs, instruction_decoder_1_rt, multiplexer_2_out;
  wire [3:0] display_driver_1_hex0, display_driver_1_hex1, instruction_decoder_1_opcode;
  wire [7:0] alu_1_result, instruction_decoder_1_immediate, multiplexer_3_out, multiplexer_4_out, ram_1_data,
       Random_result, register_file_1_read_data_1, register_file_1_read_data_2;
  wire [15:0] rom_1_data;

  PC u_PC (
    .Output(PC), .Clock(multiplexer_1_out), .IMM(instruction_decoder_1_immediate),
    .Zero(alu_1_zero_dectector), .Branch_Instruction(control_1_branch), .Jump(control_1_jump));
  Multiplexer #(.enable("false")) multiplexer_1 (
    .in0(clock_1_out), .in1(1'b0), .out(multiplexer_1_out), .sel(control_1_halt));
  Clock clock_1 (.out(clock_1_out));
  Instruction_Decoder instruction_decoder_1 (
    .Instruction(rom_1_data), .Opcode(instruction_decoder_1_opcode), .RS(instruction_decoder_1_rs),
    .RT(instruction_decoder_1_rt), .RD(instruction_decoder_1_rd), .Immediate(instruction_decoder_1_immediate));
  ROM #(.dataWidth(16)) rom_1 (.addr(PC), .data(rom_1_data));  // open: sel
  Random Random (.Clock(multiplexer_1_out), .RS(register_file_1_read_data_1), .Result(Random_result));
  Multiplexer #(.width(2), .enable("false")) multiplexer_2 (
    .in0(instruction_decoder_1_rt), .in1(instruction_decoder_1_rd), .out(multiplexer_2_out),
    .sel(control_1_w_adr));
  Control control_1 (
    .O3(instruction_decoder_1_opcode[3]), .O2(instruction_decoder_1_opcode[2]),
    .O1(instruction_decoder_1_opcode[1]), .O0(instruction_decoder_1_opcode[0]), .Branch(control_1_branch),
    .Jump(control_1_jump), .w_en(control_1_w_en), .w_adr(control_1_w_adr),
    .ALU_arg2_RAM_data_in(control_1_alu_arg2_ram_data_in), .RAM_store(control_1_ram_store),
    .RAM_load(control_1_ram_load), .put_en(control_1_put_en), .halt(control_1_halt),
    .ALU_Operation_Select(control_1_alu_operation_select),
    .Write_Data_Input_Select(control_1_write_data_input_select));
  Multiplexer #(.select(2), .width(8), .enable("false")) multiplexer_3 (
    .in0(Random_result), .in1(ram_1_data), .in2(alu_1_result), .out(multiplexer_3_out),
    .sel(control_1_write_data_input_select));  // open: in3
  Register_File register_file_1 (
    .Write_Data(multiplexer_3_out), .Write_Enable(control_1_w_en), .Read_Data_1(register_file_1_read_data_1),
    .Read_Register_1(instruction_decoder_1_rs), .Read_Data_2(register_file_1_read_data_2),
    .Read_Register_2(instruction_decoder_1_rt), .Clock(multiplexer_1_out), .Write_Address(multiplexer_2_out));
  Multiplexer #(.width(8), .enable("false")) multiplexer_4 (
    .in0(register_file_1_read_data_2), .in1(instruction_decoder_1_immediate), .out(multiplexer_4_out),
    .sel(control_1_alu_arg2_ram_data_in));
  ALU alu_1 (
    .Operand_A(register_file_1_read_data_1), .Operand_B(multiplexer_4_out), .Result(alu_1_result),
    .Zero_Dectector(alu_1_zero_dectector), .Operation_Select(control_1_alu_operation_select));  // open: Branch
  Display_Driver display_driver_1 (
    .Put_Data(register_file_1_read_data_1), .Put_Enable(control_1_put_en), .Clock(multiplexer_1_out),
    .Hex0(display_driver_1_hex0), .Hex1(display_driver_1_hex1));
  Hex_Digit_Display hex_digit_display_1 (.value(display_driver_1_hex0));  // open: dp
  Hex_Digit_Display hex_digit_display_2 (.value(display_driver_1_hex1));  // open: dp
  RAM #(.bus("separate")) ram_1 (
    .addr(alu_1_result), .din(register_file_1_read_data_2), .data(ram_1_data), .str(control_1_ram_store),
    .clk(multiplexer_1_out), .ld(control_1_ram_load));  // open: sel, clr

  // Notes on the sheet:
  //   Alex Vallejo
  //   <amv49@pitt.edu>
  //   contents of rom_1 (hex, n*v repeats v):
  //   7000 7540 e400 4201 e800 6c0 4900 4e00 ec00 9005
endmodule

module Instruction_Decoder (
  input  [15:0] Instruction,
  output [3:0] Opcode,
  output [1:0] RS,
  output [1:0] RT,
  output [1:0] RD,
  output [7:0] Immediate
);


  assign Immediate = Instruction[7:0];
  assign Opcode = Instruction[15:12];
  assign RD = Instruction[7:6];
  assign RS = Instruction[11:10];
  assign RT = Instruction[9:8];
endmodule

module Register_File (
  input  [7:0] Write_Data,
  input  Clock,
  input  Write_Enable,
  input  [1:0] Read_Register_1,
  input  [1:0] Write_Address,
  input  [1:0] Read_Register_2,
  output [7:0] Read_Data_1,
  output [7:0] Read_Data_2
);

  wire and_1_out, and_2_out, and_3_out, and_4_out, decoder_1_out0, decoder_1_out1, decoder_1_out2,
       decoder_1_out3;
  wire [7:0] R0_q, R1_q, R2_q, R3_q;

  Decoder #(.select(2)) decoder_1 (
    .out0(decoder_1_out0), .out1(decoder_1_out1), .out2(decoder_1_out2), .out3(decoder_1_out3),
    .sel(Write_Address));  // open: en
  and and_1 (and_1_out, Write_Enable, decoder_1_out0);
  and and_2 (and_2_out, Write_Enable, decoder_1_out1);
  and and_3 (and_3_out, Write_Enable, decoder_1_out2);
  and and_4 (and_4_out, Write_Enable, decoder_1_out3);
  Register R0 (.D(Write_Data), .en(and_1_out), .Q(R0_q), .clk(Clock));  // open: clr
  Register R1 (.D(Write_Data), .en(and_2_out), .Q(R1_q), .clk(Clock));  // open: clr
  Register R2 (.D(Write_Data), .en(and_3_out), .Q(R2_q), .clk(Clock));  // open: clr
  Register R3 (.D(Write_Data), .en(and_4_out), .Q(R3_q), .clk(Clock));  // open: clr
  Multiplexer #(.select(2), .width(8)) multiplexer_1 (
    .in0(R0_q), .in1(R1_q), .in2(R2_q), .in3(R3_q), .out(Read_Data_1), .sel(Read_Register_1));  // open: en
  Multiplexer #(.select(2), .width(8)) multiplexer_2 (
    .in0(R0_q), .in1(R1_q), .in2(R2_q), .in3(R3_q), .out(Read_Data_2), .sel(Read_Register_2));  // open: en
endmodule

module ALU (
  input  [7:0] Operand_A,
  input  [1:0] Operation_Select,
  input  [7:0] Operand_B,
  output [7:0] Result,
  output Branch,
  output Zero_Dectector
);

  wire comparator_1_gt, comparator_1_lt, not_1_out;
  wire [7:0] adder_1_out, bit_extender_1_out, subtractor_1_out, xor_1_out;

  assign xor_1_out = Operand_A ^ Operand_B;  // XOR_Gate xor_1, 8 bits wide
  Adder adder_1 (.a(Operand_A), .b(Operand_B), .out(adder_1_out));  // open: cin, cout
  Subtractor subtractor_1 (.a(Operand_A), .b(Operand_B), .out(subtractor_1_out));  // open: bin, bout
  Comparator comparator_1 (
    .a(Operand_A), .b({8{1'b0}}), .gt(comparator_1_gt), .eq(Zero_Dectector), .lt(comparator_1_lt));
  assign bit_extender_1_out = {{7{1'b0}}, comparator_1_lt};  // Bit_Extender bit_extender_1
  Multiplexer #(.select(2), .width(8), .enable("false")) multiplexer_1 (
    .in0(xor_1_out), .in1(adder_1_out), .in2(subtractor_1_out), .in3(bit_extender_1_out), .out(Result),
    .sel(Operation_Select));
  not not_1 (not_1_out, Zero_Dectector);
  Multiplexer #(.select(2), .enable("false")) multiplexer_2 (
    .in0(comparator_1_gt), .in1(Zero_Dectector), .in2(comparator_1_lt), .in3(not_1_out), .out(Branch),
    .sel(Operation_Select));
endmodule

module PC (
  input  [7:0] IMM,
  input  Jump,
  input  Clock,
  input  Zero,
  input  Branch_Instruction,
  output [7:0] Output
);

  wire [7:0] adder_1_out, adder_2_out, multiplexer_1_out, register_1_q, shifter_1_out;

  Adder adder_1 (.a(register_1_q), .b(8'h1), .out(adder_1_out));  // open: cin, cout
  Multiplexer #(.width(8), .enable("false")) multiplexer_1 (
    .in0(adder_1_out), .in1(IMM), .out(multiplexer_1_out), .sel(Jump));
  Register register_1 (.D(multiplexer_1_out), .Q(register_1_q), .clk(Clock));  // open: en, clr
  Adder adder_2 (.a(IMM), .b(register_1_q), .out(adder_2_out));  // open: cin, cout
  Shifter shifter_1 (.in(adder_2_out), .\dist (3'b001), .out(shifter_1_out));
  Multiplexer #(.width(8), .enable("false")) multiplexer_2 (
    .in0(register_1_q), .in1(shifter_1_out), .out(Output), .sel(1'b0));
  // AND_Gate and_1 has open pins: in0=Zero, in1=Branch_Instruction, out=open
endmodule

module Random (
  input  Clock,
  input  [7:0] RS,
  output [7:0] Result
);

  wire [7:0] rand_out, subtractor_1_out;

  Random_part \rand  (.clk(Clock), .next(1'b1), .out(rand_out));  // open: clr
  Subtractor subtractor_1 (.a(RS), .b(8'h1), .out(subtractor_1_out));  // open: bin, bout
  Divider divider_1 (.a(rand_out), .b(subtractor_1_out), .rem(Result));  // open: out, upper
endmodule

module Display_Driver (
  input  [7:0] Put_Data,
  input  Put_Enable,
  input  Clock,
  output [3:0] Hex0,
  output [3:0] Hex1
);

  Register #(.width(4)) register_1 (.D(Put_Data[3:0]), .en(Put_Enable), .Q(Hex0), .clk(Clock));  // open: clr
  Register #(.width(4)) register_2 (.D(Put_Data[7:4]), .en(Put_Enable), .Q(Hex1), .clk(Clock));  // open: clr
endmodule

module Control (
  input  O3,
  input  O2,
  input  O1,
  input  O0,
  output [1:0] ALU_Operation_Select,
  output Branch,
  output Jump,
  output w_en,
  output w_adr,
  output [1:0] Write_Data_Input_Select,
  output ALU_arg2_RAM_data_in,
  output RAM_store,
  output RAM_load,
  output put_en,
  output halt
);

  wire and_1_out, and_2_out, and_5_out, and_6_out, and_7_out, and_8_out, and_10_out, not_1_out, not_2_out,
       not_3_out, not_4_out, not_5_out, not_6_out, not_7_out, not_8_out, not_9_out, not_10_out, not_11_out,
       not_12_out, not_13_out, not_14_out, not_16_out, not_17_out, not_18_out, not_19_out, not_20_out,
       not_21_out;

  not not_1 (not_1_out, O2);
  and and_1 (and_1_out, not_1_out, O0);
  not not_2 (not_2_out, O2);
  and and_2 (and_2_out, not_2_out, O1);
  not not_3 (not_3_out, O3);
  and and_3 (ALU_Operation_Select[0], not_3_out, not_4_out);
  not not_4 (not_4_out, O0);
  not not_5 (not_5_out, O3);
  not not_6 (not_6_out, O1);
  not not_7 (not_7_out, O2);
  and and_4 (Jump, O3, not_7_out, O0);
  not not_8 (not_8_out, O3);
  and and_5 (and_5_out, not_8_out, not_9_out);
  not not_9 (not_9_out, O2);
  not not_10 (not_10_out, O3);
  and and_6 (and_6_out, not_10_out, not_11_out);
  not not_11 (not_11_out, O0);
  not not_12 (not_12_out, O3);
  and and_7 (and_7_out, not_12_out, O1);
  and and_8 (and_8_out, O3, O2, not_13_out);
  not not_13 (not_13_out, O1);
  not not_14 (not_14_out, O2);
  or or_1 (w_adr, not_14_out, O1);
  not not_15 (Write_Data_Input_Select[1], O3);
  and and_9 (Write_Data_Input_Select[0], O3, not_16_out);
  not not_16 (not_16_out, O0);
  and and_10 (and_10_out, O2, not_17_out);
  not not_17 (not_17_out, O1);
  not not_18 (not_18_out, O2);
  and and_11 (RAM_store, O3, not_18_out, not_19_out);
  not not_19 (not_19_out, O0);
  not not_20 (not_20_out, O1);
  not not_21 (not_21_out, O0);
  and and_12 (put_en, O3, O1);
  and and_13 (halt, O0, O1, O2, O3);
  or or_2 (ALU_Operation_Select[1], and_1_out, and_2_out, O3);
  and and_14 (Branch, not_5_out, O2, not_6_out, O0);
  or or_3 (w_en, and_5_out, and_6_out, and_7_out, and_8_out);
  or or_4 (ALU_arg2_RAM_data_in, and_10_out, O3);
  and and_15 (RAM_load, O3, O2, not_20_out, not_21_out);
endmodule
